// Logisim project lc3.circ as structural Verilog
module microseq_mux (
  input  IRD,
  input  ZERO,
  input  ZERO_2,
  input  IR12,
  input  IR13,
  input  IR14,
  input  IR15,
  input  j0,
  input  j1,
  input  j2,
  input  j3,
  input  j4,
  input  in_13,
  output out_14,
  output out_15,
  output out_16,
  output out_17,
  output out_18,
  output out_19
);

  wire and_1_out, and_2_out, and_3_out, and_4_out, and_5_out, and_6_out, and_7_out, and_8_out, and_9_out,
       and_10_out, and_11_out, and_12_out, not_1_out;

  not not_1 (not_1_out, IRD);
  and and_1 (and_1_out, IRD, ZERO);
  buf and_2 (and_2_out, ZERO_2);  // AND_Gate
  and and_3 (and_3_out, IR12, IRD);
  and and_4 (and_4_out, IR13, IRD);
  buf and_5 (and_5_out, IR14);  // AND_Gate
  and and_6 (and_6_out, IR15, IRD);
  and and_7 (and_7_out, not_1_out, j0);
  and and_8 (and_8_out, not_1_out, j1);
  and and_9 (and_9_out, not_1_out, j2);
  and and_10 (and_10_out, not_1_out, j3);
  and and_11 (and_11_out, not_1_out, j4);
  and and_12 (and_12_out, in_13, not_1_out);
  or or_1 (out_14, and_1_out, and_7_out);
  or or_2 (out_15, and_8_out, and_2_out);
  or or_3 (out_16, and_3_out, and_9_out);
  or or_4 (out_17, and_4_out, and_10_out);
  or or_5 (out_18, and_5_out, and_11_out);
  or or_6 (out_19, and_6_out, and_12_out);
endmodule

module main (
  output [15:0] out_1
);

  wire ADDR1MUX, button_1_out, CLK, clock_1_out, GateALU, GateMARMUX, GateMDR, GatePC, GatePC_1, GatePSR,
       GateSP, GateVector, LD_BEN, LD_CC, LD_IR, LD_MAR, LD_MDR, LD_PC, LD_Priv, LD_REG, LD_SavedSSP,
       LD_SavedUSP, LD_Vector, logic_1_n, logic_1_p, logic_1_z, MARMUX, memory_1_r, MIO_EN, N_q, not_1_out,
       P_q, PSRMUX, R_W, register_1_q, Set_Priv, SR2MUX, Z_q;
  wire [1:0] ADDR2MUX, ALUK, DRMUX, PCMUX, SPMUX, SR1MUX, VectorMUX;
  wire [2:0] DR, SR1, SR2;
  wire [4:0] bitselector_5_out;
  wire [5:0] bitselector_4_out;
  wire [7:0] bitselector_1_out;
  wire [8:0] bitselector_3_out;
  wire [10:0] bitselector_2_out;
  wire [15:0] adder_1_out, adder_2_out, alu_1_aluout, bit_extender_1_out, bit_extender_2_out,
       bit_extender_3_out, bit_extender_4_out, bit_extender_5_out, buffer_1_out, controlled_buffer_1_out,
       controlled_buffer_4_out, controlled_buffer_5_out, controlled_buffer_7_out, IR_q, memory_1_bus_out,
       multiplexer_1_out, multiplexer_2_out, multiplexer_3_out, multiplexer_4_out, multiplexer_5_out, PC_q,
       regfile_1_out_8, regfile_1_sr1out;

  Clock clock_1 (.out(clock_1_out));
  Register #(.width(1)) register_1 (
    .D(not_1_out), .en(button_1_out), .Q(register_1_q), .clk(button_1_out));  // open: clr
  Button button_1 (.out(button_1_out));
  and and_1 (CLK, clock_1_out, register_1_q);
  not not_1 (not_1_out, register_1_q);
  assign buffer_1_out = out_1;  // Buffer buffer_1, 16 bits wide
  assign controlled_buffer_1_out = CLK ? out_1 : 16'bz;  // Controlled_Buffer controlled_buffer_1
  Register #(.width(16)) IR (.D(buffer_1_out), .en(LD_IR), .Q(IR_q), .clk(CLK));  // open: clr
  assign out_1 = GateMDR ? memory_1_bus_out : 16'bz;  // Controlled_Buffer controlled_buffer_2
  memory memory_1 (
    .BUS_IN(controlled_buffer_1_out), .CLK(CLK), .LD_MAR(LD_MAR), .R_W(R_W), .MIO_EN(MIO_EN),
    .LD_MDR(LD_MDR), .R(memory_1_r), .BUS_OUT(memory_1_bus_out));
  Register #(.width(1)) N (.D(logic_1_n), .en(LD_CC), .Q(N_q), .clk(CLK));  // open: clr
  Register #(.width(1)) Z (.D(logic_1_z), .en(LD_CC), .Q(Z_q), .clk(CLK));  // open: clr
  Register #(.width(1)) P (.D(logic_1_p), .en(LD_CC), .Q(P_q), .clk(CLK));  // open: clr
  BitSelector #(.width(16), .group(8)) bitselector_1 (.in(IR_q), .out(bitselector_1_out));  // open: sel
  assign out_1 = GateMARMUX ? multiplexer_1_out : 16'bz;  // Controlled_Buffer controlled_buffer_3
  Multiplexer #(.width(16), .enable("false")) multiplexer_1 (
    .in0(bit_extender_1_out), .in1(adder_1_out), .out(multiplexer_1_out), .sel(MARMUX));
  assign bit_extender_1_out = {{8{1'b0}}, bitselector_1_out};  // Bit_Extender bit_extender_1
  assign bit_extender_2_out = {{5{1'b0}}, bitselector_2_out};  // Bit_Extender bit_extender_2
  BitSelector #(.width(16), .group(11)) bitselector_2 (.in(IR_q), .out(bitselector_2_out));  // open: sel
  BitSelector #(.width(16), .group(9)) bitselector_3 (.in(IR_q), .out(bitselector_3_out));  // open: sel
  assign bit_extender_3_out = {{7{bitselector_3_out[8]}}, bitselector_3_out};  // Bit_Extender bit_extender_3
  assign bit_extender_4_out = {{10{bitselector_4_out[5]}}, bitselector_4_out};  // Bit_Extender bit_extender_4
  BitSelector #(.width(16), .group(6)) bitselector_4 (.in(IR_q), .out(bitselector_4_out));  // open: sel
  assign controlled_buffer_4_out = CLK ? out_1 : 16'bz;  // Controlled_Buffer controlled_buffer_4
  LOGIC logic_1 (.BUS_IN(controlled_buffer_4_out), .N(logic_1_n), .Z(logic_1_z), .P(logic_1_p));
  assign controlled_buffer_5_out = CLK ? out_1 : 16'bz;  // Controlled_Buffer controlled_buffer_5
  BitSelector #(.width(16), .group(5)) bitselector_5 (.in(IR_q), .out(bitselector_5_out));  // open: sel
  assign out_1 = GatePC ? PC_q : 16'bz;  // Controlled_Buffer controlled_buffer_6
  Register #(.width(16)) PC (.D(multiplexer_2_out), .en(LD_PC), .Q(PC_q), .clk(CLK));  // open: clr
  Multiplexer #(.select(2), .width(16), .enable("false")) multiplexer_2 (
    .in0(controlled_buffer_5_out), .in1(adder_1_out), .in2(adder_2_out), .out(multiplexer_2_out), .sel(PCMUX));  // open: in3
  Multiplexer #(.select(2), .width(16), .enable("false")) multiplexer_3 (
    .in0({16{1'b0}}), .in1(bit_extender_2_out), .in2(bit_extender_3_out), .in3(bit_extender_4_out),
    .out(multiplexer_3_out), .sel(ADDR2MUX));
  assign bit_extender_5_out = {{11{1'b0}}, bitselector_5_out};  // Bit_Extender bit_extender_5
  Control control_1 (
    .IR(IR_q), .R(memory_1_r), .P(P_q), .Z(Z_q), .N(N_q), .LD_MAR(LD_MAR), .LD_MDR(LD_MDR), .LD_IR(LD_IR),
    .LD_BEN(LD_BEN), .LD_REG(LD_REG), .LD_CC(LD_CC), .LD_PC(LD_PC), .LD_Priv(LD_Priv),
    .LD_SavedSSP(LD_SavedSSP), .LD_SavedUSP(LD_SavedUSP), .LD_Vector(LD_Vector), .GatePC(GatePC),
    .GateMDR(GateMDR), .GateALU(GateALU), .GateMARMUX(GateMARMUX), .GateVector(GateVector),
    .GatePC_1(GatePC_1), .GatePSR(GatePSR), .GateSP(GateSP), .PCMUX(PCMUX), .DRMUX(DRMUX), .SR1MUX(SR1MUX),
    .ADDR1MUX(ADDR1MUX), .ADDR2MUX(ADDR2MUX), .SPMUX(SPMUX), .MARMUX(MARMUX), .VectorMUX(VectorMUX),
    .PSRMUX(PSRMUX), .ALUK(ALUK), .MIO_EN(MIO_EN), .R_W(R_W), .Set_Priv(Set_Priv));  // open: PSR_15, INT
  Adder #(.width(16)) adder_1 (.a(multiplexer_3_out), .b(multiplexer_4_out), .out(adder_1_out));  // open: cin, cout
  Multiplexer #(.width(16), .enable("false")) multiplexer_4 (
    .in0(regfile_1_sr1out), .in1(PC_q), .out(multiplexer_4_out), .sel(ADDR1MUX));
  assign controlled_buffer_7_out = CLK ? out_1 : 16'bz;  // Controlled_Buffer controlled_buffer_7
  Adder #(.width(16)) adder_2 (.a(16'h1), .b(PC_q), .out(adder_2_out));  // open: cin, cout
  REGFILE regfile_1 (
    .BUS_IN(controlled_buffer_7_out), .DR(DR), .LD_REG(LD_REG), .SR1(SR1), .SR2(SR2), .CLK(CLK),
    .SR1OUT(regfile_1_sr1out), .out_8(regfile_1_out_8));
  Multiplexer #(.width(16), .enable("false")) multiplexer_5 (
    .in0(bit_extender_5_out), .in1(regfile_1_out_8), .out(multiplexer_5_out), .sel(SR2MUX));
  ALU alu_1 (.SR1IN(regfile_1_sr1out), .SR2IN(multiplexer_5_out), .ALUK(ALUK), .ALUOUT(alu_1_aluout));  // open: C_out
  assign out_1 = GateALU ? alu_1_aluout : 16'bz;  // Controlled_Buffer controlled_buffer_8

  // Notes on the sheet:
  //   [10:0]
  //   [8:0]
  //   [5:0]
  //   [0:4]
  //   LOGIC
  //   ADDR ADDER
endmodule

module microsequencer (
  input  IRD,
  input  ir12,
  input  ir13,
  input  ir14,
  input  _15,
  input  j0,
  input  j1,
  input  j2,
  input  j3,
  input  j4,
  input  j5,
  input  cond0,
  input  cond1,
  input  cond2,
  input  INT,
  input  R,
  input  PSR15,
  input  BEN,
  input  IR11,
  output a0,
  output a1,
  output a2,
  output a3,
  output a4,
  output a5
);

  wire and_1_out, and_2_out, and_3_out, and_4_out, and_5_out, and_6_out, not_1_out, not_2_out, not_3_out,
       not_4_out, not_5_out, not_6_out, not_7_out, or_1_out, or_2_out, or_3_out, or_4_out, or_5_out;

  not not_1 (not_1_out, ir12);
  not not_2 (not_2_out, cond2);
  and and_1 (and_1_out, not_1_out, ir12);
  not not_3 (not_3_out, cond1);
  not not_4 (not_4_out, cond0);
  not not_5 (not_5_out, cond1);
  and and_2 (and_2_out, IR11, cond1, cond0, not_2_out);
  and and_3 (and_3_out, cond0, R, not_6_out, not_2_out);
  not not_6 (not_6_out, cond0);
  not not_7 (not_7_out, cond2);
  and and_4 (and_4_out, not_6_out, not_7_out, cond1, BEN);
  and and_5 (and_5_out, not_3_out, not_4_out, cond2, PSR15);
  and and_6 (and_6_out, not_5_out, cond2, cond0, INT);
  or or_1 (or_1_out, and_2_out, j0);
  or or_2 (or_2_out, and_3_out, j1);
  or or_3 (or_3_out, and_4_out, j2);
  or or_4 (or_4_out, and_5_out, j3);
  or or_5 (or_5_out, j4, and_6_out);
  microseq_mux microseq_mux_1 (
    .IRD(IRD), .ZERO(and_1_out), .ZERO_2(and_1_out), .IR12(ir12), .IR13(ir13), .IR14(ir14), .IR15(_15),
    .j0(or_1_out), .j1(or_2_out), .j2(or_3_out), .j3(or_4_out), .j4(or_5_out), .in_13(j5), .out_14(a0),
    .out_15(a1), .out_16(a2), .out_17(a3), .out_18(a4), .out_19(a5));
endmodule

module memory (
  input  [15:0] BUS_IN,
  input  CLK,
  input  MIO_EN,
  input  LD_MDR,
  input  LD_MAR,
  input  R_W,
  output R,
  output [15:0] BUS_OUT
);

  wire addr_ctrl_logic_1_ld_ddr, addr_ctrl_logic_1_ld_dsr, addr_ctrl_logic_1_ld_kbsr,
       addr_ctrl_logic_1_mem_en, and_1_out, and_2_out, not_1_out, not_2_out;
  wire [1:0] addr_ctrl_logic_1_inmux_sel;
  wire [15:0] buffer_1_out, DSR_q, KBDR_q, KBSR_q, MAR_q, multiplexer_1_out, multiplexer_2_out, ram_1_data;

  Register #(.width(16)) MAR (.D(BUS_IN), .en(LD_MAR), .Q(MAR_q), .clk(CLK));  // open: clr
  and and_1 (and_1_out, R_W, addr_ctrl_logic_1_mem_en);
  not not_1 (not_1_out, R_W);
  RAM #(.addrWidth(16), .dataWidth(16), .bus("separate")) ram_1 (
    .addr(MAR_q), .din(BUS_OUT), .data(ram_1_data), .str(and_1_out), .clk(CLK), .ld(and_2_out));  // open: sel, clr
  and and_2 (and_2_out, not_1_out, addr_ctrl_logic_1_mem_en);
  Multiplexer #(.width(16), .enable("false")) multiplexer_1 (
    .in0(multiplexer_2_out), .in1(BUS_IN), .out(multiplexer_1_out), .sel(not_2_out));
  not not_2 (not_2_out, MIO_EN);
  Multiplexer #(.select(2), .width(16), .enable("false")) multiplexer_2 (
    .in0(ram_1_data), .in1(KBSR_q), .in2(KBDR_q), .in3(DSR_q), .out(multiplexer_2_out),
    .sel(addr_ctrl_logic_1_inmux_sel));
  Register #(.width(16)) MDR (.D(multiplexer_1_out), .en(CLK), .Q(BUS_OUT), .clk(LD_MDR));  // open: clr
  addr_ctrl_logic addr_ctrl_logic_1 (
    .MIO_EN(MIO_EN), .R_W(R_W), .MAR(MAR_q), .MEM_EN(addr_ctrl_logic_1_mem_en),
    .LD_KBSR(addr_ctrl_logic_1_ld_kbsr), .LD_DSR(addr_ctrl_logic_1_ld_dsr),
    .LD_DDR(addr_ctrl_logic_1_ld_ddr), .INMUX_SEL(addr_ctrl_logic_1_inmux_sel));
  assign buffer_1_out = BUS_OUT;  // Buffer buffer_1, 16 bits wide
  Register #(.width(16)) KBDR (.D(buffer_1_out), .Q(KBDR_q), .clk(CLK));  // open: en, clr
  Register #(.width(16)) KBSR (.D(buffer_1_out), .en(addr_ctrl_logic_1_ld_kbsr), .Q(KBSR_q), .clk(CLK));  // open: clr
  Register #(.width(16)) DDR (.D(buffer_1_out), .en(addr_ctrl_logic_1_ld_ddr), .clk(CLK));  // open: Q, clr
  Register #(.width(16)) DSR (.D(buffer_1_out), .en(addr_ctrl_logic_1_ld_dsr), .Q(DSR_q), .clk(CLK));  // open: clr
endmodule

module addr_ctrl_logic (
  input  MIO_EN,
  input  R_W,
  input  [15:0] MAR,
  output LD_KBSR,
  output MEM_EN,
  output LD_DSR,
  output LD_DDR,
  output [1:0] INMUX_SEL
);

  wire and_1_out, and_2_out, and_3_out, and_4_out, and_5_out, and_7_out, and_9_out, and_10_out, and_11_out,
       decoder_1_out15, decoder_2_out14, decoder_3_out0, decoder_4_out0, decoder_4_out2, decoder_4_out4,
       decoder_4_out6, nor_1_out, not_1_out, not_2_out, or_1_out, or_3_out;
  wire [1:0] adder_1_out, adder_2_out, adder_3_out, bit_extender_1_out, bit_extender_2_out,
       bit_extender_3_out, or_2_out;
  wire [3:0] bitselector_3_out, bitselector_4_out, bitselector_5_out, bitselector_6_out;
  wire [7:0] bitselector_1_out, bitselector_2_out;

  BitSelector #(.width(16), .group(8)) bitselector_1 (.in(MAR), .out(bitselector_1_out), .sel(1'b1));
  BitSelector #(.width(16), .group(8)) bitselector_2 (.in(MAR), .out(bitselector_2_out), .sel(1'b0));
  BitSelector #(.group(4)) bitselector_3 (.in(bitselector_1_out), .out(bitselector_3_out), .sel(1'b1));
  Decoder #(.select(4), .enable("false")) decoder_1 (
    .out15(decoder_1_out15), .sel(bitselector_3_out));  // open: out0, out1, out2, out3, out4, out5, out6, out7, out8, out9, out10, out11, out12, out13, out14
  Decoder #(.select(4), .enable("false")) decoder_2 (
    .out14(decoder_2_out14), .sel(bitselector_4_out));  // open: out0, out1, out2, out3, out4, out5, out6, out7, out8, out9, out10, out11, out12, out13, out15
  BitSelector #(.group(4)) bitselector_4 (.in(bitselector_1_out), .out(bitselector_4_out), .sel(1'b0));
  BitSelector #(.group(4)) bitselector_5 (.in(bitselector_2_out), .out(bitselector_5_out), .sel(1'b1));
  Decoder #(.select(4), .enable("false")) decoder_3 (
    .out0(decoder_3_out0), .sel(bitselector_5_out));  // open: out1, out2, out3, out4, out5, out6, out7, out8, out9, out10, out11, out12, out13, out14, out15
  BitSelector #(.group(4)) bitselector_6 (.in(bitselector_2_out), .out(bitselector_6_out), .sel(1'b0));
  Decoder #(.select(4), .enable("false")) decoder_4 (
    .out0(decoder_4_out0), .out2(decoder_4_out2), .out4(decoder_4_out4), .out6(decoder_4_out6),
    .sel(bitselector_6_out));  // open: out1, out3, out5, out7, out8, out9, out10, out11, out12, out13, out14, out15
  not not_1 (not_1_out, R_W);
  not not_2 (not_2_out, and_1_out);
  and and_1 (and_1_out, decoder_1_out15, decoder_2_out14, decoder_3_out0);
  nor nor_1 (nor_1_out, decoder_4_out0, decoder_4_out2, decoder_4_out4, decoder_4_out6);
  or or_1 (or_1_out, not_2_out, nor_1_out);
  and and_2 (and_2_out, decoder_4_out0, and_1_out);
  and and_3 (and_3_out, and_1_out, decoder_4_out2);
  and and_4 (and_4_out, and_1_out, decoder_4_out4);
  and and_5 (and_5_out, and_1_out, decoder_4_out6);
  and and_6 (MEM_EN, MIO_EN, or_1_out);
  and and_7 (and_7_out, or_1_out, MIO_EN, not_1_out);
  and and_8 (LD_KBSR, ~not_1_out, MIO_EN, and_2_out);  // AND_Gate
  and and_9 (and_9_out, MIO_EN, not_1_out, and_2_out);
  and and_10 (and_10_out, not_1_out, MIO_EN, and_3_out);
  and and_11 (and_11_out, not_1_out, MIO_EN, and_4_out);
  and and_12 (LD_DSR, ~not_1_out, and_4_out, MIO_EN);  // AND_Gate
  and and_13 (LD_DDR, and_5_out, ~not_1_out, MIO_EN);  // AND_Gate
  assign bit_extender_1_out = {{1{1'b0}}, and_9_out};  // Bit_Extender bit_extender_1
  assign bit_extender_2_out = {{1{1'b0}}, and_10_out};  // Bit_Extender bit_extender_2
  assign bit_extender_3_out = {{1{1'b0}}, and_11_out};  // Bit_Extender bit_extender_3
  Adder #(.width(2)) adder_1 (.a(bit_extender_2_out), .b(bit_extender_2_out), .out(adder_1_out));  // open: cin, cout
  Adder #(.width(2)) adder_2 (.a(bit_extender_3_out), .b(bit_extender_3_out), .out(adder_2_out));  // open: cin, cout
  Adder #(.width(2)) adder_3 (.a(bit_extender_3_out), .b(adder_2_out), .out(adder_3_out));  // open: cin, cout
  assign or_2_out = adder_1_out | adder_3_out | bit_extender_1_out;  // OR_Gate or_2, 2 bits wide
  assign INMUX_SEL = or_3_out ? or_2_out : 2'bz;  // Controlled_Buffer controlled_buffer_1
  or or_3 (or_3_out, and_9_out, and_7_out, and_10_out, and_11_out);

  // Notes on the sheet:
  //   FE04
  //   FE06
  //   FE00
  //   FE02
  //   00 = mem
  //   01 = KBSR
  //   10 = KBDR
  //   11 = DSR
endmodule

module REGFILE (
  input  [15:0] BUS_IN,
  input  [2:0] DR,
  input  LD_REG,
  input  [2:0] SR1,
  input  [2:0] SR2,
  input  CLK,
  output [15:0] SR1OUT,
  output [15:0] out_8
);

  wire and_1_out, and_2_out, and_3_out, and_4_out, and_5_out, and_6_out, and_7_out, and_8_out,
       decoder_1_out0, decoder_1_out1, decoder_1_out2, decoder_1_out3, decoder_1_out4, decoder_1_out5,
       decoder_1_out6, decoder_1_out7;
  wire [15:0] R0_q, R1_q, R2_q, R3_q, R4_q, R5_q, R6_q, R7_q;

  Decoder #(.select(3), .enable("false")) decoder_1 (
    .out0(decoder_1_out0), .out1(decoder_1_out1), .out2(decoder_1_out2), .out3(decoder_1_out3),
    .out4(decoder_1_out4), .out5(decoder_1_out5), .out6(decoder_1_out6), .out7(decoder_1_out7), .sel(DR));
  and and_1 (and_1_out, decoder_1_out0, LD_REG);
  and and_2 (and_2_out, decoder_1_out4, LD_REG);
  Register #(.width(16)) R0 (.D(BUS_IN), .en(and_1_out), .Q(R0_q), .clk(CLK));  // open: clr
  Register #(.width(16)) R4 (.D(BUS_IN), .en(and_2_out), .Q(R4_q), .clk(CLK));  // open: clr
  and and_3 (and_3_out, decoder_1_out1, LD_REG);
  and and_4 (and_4_out, decoder_1_out5, LD_REG);
  Register #(.width(16)) R1 (.D(BUS_IN), .en(and_3_out), .Q(R1_q), .clk(CLK));  // open: clr
  Register #(.width(16)) R5 (.D(BUS_IN), .en(and_4_out), .Q(R5_q), .clk(CLK));  // open: clr
  and and_5 (and_5_out, decoder_1_out2, LD_REG);
  and and_6 (and_6_out, decoder_1_out6, LD_REG);
  Register #(.width(16)) R2 (.D(BUS_IN), .en(and_5_out), .Q(R2_q), .clk(CLK));  // open: clr
  Register #(.width(16)) R6 (.D(BUS_IN), .en(and_6_out), .Q(R6_q), .clk(CLK));  // open: clr
  and and_7 (and_7_out, decoder_1_out7, LD_REG);
  Register #(.width(16)) R3 (.D(BUS_IN), .en(and_8_out), .Q(R3_q), .clk(CLK));  // open: clr
  and and_8 (and_8_out, decoder_1_out3, LD_REG);
  Register #(.width(16)) R7 (.D(BUS_IN), .en(and_7_out), .Q(R7_q), .clk(CLK));  // open: clr
  Multiplexer #(.select(3), .width(16), .enable("false")) multiplexer_1 (
    .in0(R0_q), .in1(R1_q), .in2(R2_q), .in3(R3_q), .in4(R4_q), .in5(R5_q), .in6(R6_q), .in7(R7_q),
    .out(out_8), .sel(SR2));
  Multiplexer #(.select(3), .width(16), .enable("false")) multiplexer_2 (
    .in0(R0_q), .in1(R1_q), .in2(R2_q), .in3(R3_q), .in4(R4_q), .in5(R5_q), .in6(R6_q), .in7(R7_q),
    .out(SR1OUT), .sel(SR1));

  // Notes on the sheet:
  //   SR2OUT
endmodule

module ALU (
  input  [15:0] SR1IN,
  input  [15:0] SR2IN,
  input  [1:0] ALUK,
  output [15:0] ALUOUT,
  output C_out
);

  wire [15:0] adder_1_out, and_1_out, not_1_out;

  assign and_1_out = SR1IN & SR2IN;  // AND_Gate and_1, 16 bits wide
  Adder #(.width(16)) adder_1 (.a(SR1IN), .b(SR2IN), .out(adder_1_out), .cout(C_out));  // open: cin
  assign not_1_out = ~SR1IN;  // NOT_Gate not_1, 16 bits wide
  Multiplexer #(.select(2), .width(16), .enable("false")) multiplexer_1 (
    .in0(adder_1_out), .in1(and_1_out), .in2(not_1_out), .in3(SR1IN), .out(ALUOUT), .sel(ALUK));
endmodule

module Control (
  input  [15:0] IR,
  input  PSR_15,
  input  INT,
  input  R,
  input  P,
  input  Z,
  input  N,
  output LD_MAR,
  output LD_MDR,
  output LD_IR,
  output LD_BEN,
  output LD_REG,
  output LD_CC,
  output LD_PC,
  output LD_Priv,
  output LD_SavedSSP,
  output LD_SavedUSP,
  output LD_Vector,
  output GatePC,
  output GateMDR,
  output GateALU,
  output GateMARMUX,
  output GateVector,
  output GatePC_1,
  output GatePSR,
  output GateSP,
  output [1:0] PCMUX,
  output [1:0] DRMUX,
  output [1:0] SR1MUX,
  output ADDR1MUX,
  output [1:0] ADDR2MUX,
  output [1:0] SPMUX,
  output MARMUX,
  output [1:0] VectorMUX,
  output PSRMUX,
  output [1:0] ALUK,
  output MIO_EN,
  output R_W,
  output Set_Priv
);

  wire and_1_out, and_2_out, and_3_out, bitselector_1_out, bitselector_2_out, bitselector_3_out,
       microsequencer_1_a0, microsequencer_1_a1, microsequencer_1_a2, microsequencer_1_a3,
       microsequencer_1_a4, microsequencer_1_a5, or_1_out;
  wire [3:0] bitselector_4_out;
  wire [16:0] control_store_1_out2;
  wire [16:7] buffer_2_out;
  wire [31:0] control_store_1_out1;

  BitSelector #(.width(16)) bitselector_1 (.in(IR), .out(bitselector_1_out), .sel(4'b1010));
  BitSelector #(.width(16)) bitselector_2 (.in(IR), .out(bitselector_2_out), .sel(4'b1001));
  and and_1 (and_1_out, bitselector_2_out, P);
  BitSelector #(.width(16)) bitselector_3 (.in(IR), .out(bitselector_3_out), .sel(4'b1011));
  and and_2 (and_2_out, bitselector_1_out, Z);
  and and_3 (and_3_out, bitselector_3_out, N);
  BitSelector #(.width(16), .group(4)) bitselector_4 (.in(IR), .out(bitselector_4_out), .sel(2'b11));
  or or_1 (or_1_out, and_1_out, and_2_out, and_3_out);
  microsequencer microsequencer_1 (
    .IRD(buffer_2_out[7]), .ir12(bitselector_4_out[0]), .ir13(bitselector_4_out[1]),
    .ir14(bitselector_4_out[2]), ._15(bitselector_4_out[3]), .j0(buffer_2_out[16]), .j1(buffer_2_out[15]),
    .j2(buffer_2_out[14]), .j3(buffer_2_out[13]), .j4(buffer_2_out[12]), .j5(buffer_2_out[11]),
    .cond0(buffer_2_out[10]), .cond1(buffer_2_out[9]), .cond2(buffer_2_out[8]), .INT(INT), .R(R),
    .PSR15(PSR_15), .BEN(or_1_out), .IR11(bitselector_3_out), .a0(microsequencer_1_a0),
    .a1(microsequencer_1_a1), .a2(microsequencer_1_a2), .a3(microsequencer_1_a3), .a4(microsequencer_1_a4),
    .a5(microsequencer_1_a5));
  assign {VectorMUX[1], MARMUX, SPMUX[0], SPMUX[1], ADDR2MUX[0], ADDR2MUX[1], ADDR1MUX, SR1MUX[0], SR1MUX[1], DRMUX[0], DRMUX[1], PCMUX[0], PCMUX[1], GateSP, GatePSR, GatePC_1, GateVector, GateMARMUX, GateALU, GateMDR, GatePC, LD_Vector, LD_SavedUSP, LD_SavedSSP, LD_Priv, LD_PC, LD_CC, LD_REG, LD_BEN, LD_IR, LD_MDR, LD_MAR} = control_store_1_out1;  // Buffer buffer_1, 32 bits wide
  Control_Store control_store_1 (
    .a0(microsequencer_1_a0), .a1(microsequencer_1_a1), .a2(microsequencer_1_a2), .a3(microsequencer_1_a3),
    .a4(microsequencer_1_a4), .a5(microsequencer_1_a5), .out1(control_store_1_out1),
    .out2(control_store_1_out2));
  assign {buffer_2_out, Set_Priv, R_W, MIO_EN, ALUK[0], ALUK[1], PSRMUX, VectorMUX[0]} = control_store_1_out2;  // Buffer buffer_2, 17 bits wide

  // Notes on the sheet:
  //   byte2
  //   byte3
  //   byte4
  //   byte1
endmodule

module LOGIC (
  input  [15:0] BUS_IN,
  output N,
  output Z,
  output P
);

  wire comparator_1_eq, comparator_1_gt, not_1_out;
  wire [14:0] bit_extender_1_out, bitselector_1_out;

  BitSelector #(.width(16), .group(15)) bitselector_1 (.in(BUS_IN), .out(bitselector_1_out), .sel(1'b0));
  assign bit_extender_1_out = {{14{1'b0}}, 1'b0};  // Bit_Extender bit_extender_1
  BitSelector #(.width(16)) bitselector_2 (.in(BUS_IN), .out(N), .sel(4'b1111));
  not not_1 (not_1_out, N);
  Comparator #(.width(15)) comparator_1 (
    .a(bitselector_1_out), .b(bit_extender_1_out), .gt(comparator_1_gt), .eq(comparator_1_eq));  // open: lt
  and and_1 (P, not_1_out, comparator_1_gt);
  and and_2 (Z, not_1_out, comparator_1_eq);
endmodule

module Control_Store (
  input  a0,
  input  a1,
  input  a2,
  input  a3,
  input  a4,
  input  a5,
  output [31:0] out1,
  output [16:0] out2
);

  wire [16:0] _0a, _1a, _2a, _3a, _4a, _5a, _6a, _7a, _8a, _9a, _10a, _11a, _12a, _13a, _14a, _15a, _16a,
       _17a, _18a, _19a, _20a, _21a, _22a, _23a, _24a, _25a, _26a, _27a, _28a, _29a, _30a, _31a, _32a, _33a,
       _34a, _35a, _36a, _37a, _38a, _39a, _40a, _41a, _42a, _43a, _44a, _45a, _46a, _47a, _48a, _49a, _50a,
       _51a, _52a, _53a, _54a, _55a, _56a, _57a, _58a, _59a, _60a, _61a, _62a, _63a, multiplexer_4_out,
       multiplexer_5_out;
  wire [31:0] _0, _1, _2, _3, _4, _5, _6, _7, _8, _9, _10, _11, _12, _13, _14, _15, _16, _17, _18, _19, _20,
       _21, _22, _23, _24, _25, _26, _27, _28, _29, _30, _31, _32, _33, _34, _35, _36, _37, _38, _39, _40,
       _41, _42, _43, _44, _45, _46, _47, _48, _49, _50, _51, _52, _53, _54, _55, _56, _57, _58, _59, _60,
       _61, _62, _63, multiplexer_1_out, multiplexer_2_out;

  Register #(.width(32)) register_1 (.Q(_0));  // open: D, en, clk, clr
  Register #(.width(17)) register_2 (.Q(_0a));  // open: D, en, clk, clr
  Register #(.width(32)) register_3 (.Q(_8));  // open: D, en, clk, clr
  Register #(.width(17)) register_4 (.Q(_8a));  // open: D, en, clk, clr
  Register #(.width(32)) register_5 (.Q(_16));  // open: D, en, clk, clr
  Register #(.width(17)) register_6 (.Q(_16a));  // open: D, en, clk, clr
  Register #(.width(32)) register_7 (.Q(_24));  // open: D, en, clk, clr
  Register #(.width(17)) register_8 (.Q(_24a));  // open: D, en, clk, clr
  Register #(.width(32)) register_9 (.Q(_32));  // open: D, en, clk, clr
  Register #(.width(17)) register_10 (.Q(_32a));  // open: D, en, clk, clr
  Register #(.width(32)) register_11 (.Q(_39));  // open: D, en, clk, clr
  Register #(.width(17)) register_12 (.Q(_39a));  // open: D, en, clk, clr
  Register #(.width(32)) register_13 (.Q(_46));  // open: D, en, clk, clr
  Register #(.width(17)) register_14 (.Q(_46a));  // open: D, en, clk, clr
  Register #(.width(32)) register_15 (.Q(_53));  // open: D, en, clk, clr
  Register #(.width(17)) register_16 (.Q(_53a));  // open: D, en, clk, clr
  Register #(.width(32)) register_17 (.Q(_1));  // open: D, en, clk, clr
  Register #(.width(17)) register_18 (.Q(_1a));  // open: D, en, clk, clr
  Register #(.width(32)) register_19 (.Q(_9));  // open: D, en, clk, clr
  Register #(.width(17)) register_20 (.Q(_9a));  // open: D, en, clk, clr
  Register #(.width(32)) register_21 (.Q(_17));  // open: D, en, clk, clr
  Register #(.width(17)) register_22 (.Q(_17a));  // open: D, en, clk, clr
  Register #(.width(32)) register_23 (.Q(_25));  // open: D, en, clk, clr
  Register #(.width(17)) register_24 (.Q(_25a));  // open: D, en, clk, clr
  Register #(.width(32)) register_25 (.Q(_33));  // open: D, en, clk, clr
  Register #(.width(17)) register_26 (.Q(_33a));  // open: D, en, clk, clr
  Register #(.width(32)) register_27 (.Q(_40));  // open: D, en, clk, clr
  Register #(.width(17)) register_28 (.Q(_40a));  // open: D, en, clk, clr
  Register #(.width(32)) register_29 (.Q(_47));  // open: D, en, clk, clr
  Register #(.width(17)) register_30 (.Q(_47a));  // open: D, en, clk, clr
  Register #(.width(32)) register_31 (.Q(_54));  // open: D, en, clk, clr
  Register #(.width(17)) register_32 (.Q(_54a));  // open: D, en, clk, clr
  Register #(.width(32)) register_33 (.Q(_2));  // open: D, en, clk, clr
  Register #(.width(17)) register_34 (.Q(_2a));  // open: D, en, clk, clr
  Register #(.width(32)) register_35 (.Q(_10));  // open: D, en, clk, clr
  Register #(.width(17)) register_36 (.Q(_10a));  // open: D, en, clk, clr
  Register #(.width(32)) register_37 (.Q(_18));  // open: D, en, clk, clr
  Register #(.width(17)) register_38 (.Q(_18a));  // open: D, en, clk, clr
  Register #(.width(32)) register_39 (.Q(_26));  // open: D, en, clk, clr
  Register #(.width(17)) register_40 (.Q(_26a));  // open: D, en, clk, clr
  Register #(.width(32)) register_41 (.Q(_34));  // open: D, en, clk, clr
  Register #(.width(17)) register_42 (.Q(_34a));  // open: D, en, clk, clr
  Register #(.width(32)) register_43 (.Q(_41));  // open: D, en, clk, clr
  Register #(.width(17)) register_44 (.Q(_41a));  // open: D, en, clk, clr
  Register #(.width(32)) register_45 (.Q(_48));  // open: D, en, clk, clr
  Register #(.width(17)) register_46 (.Q(_48a));  // open: D, en, clk, clr
  Register #(.width(32)) register_47 (.Q(_55));  // open: D, en, clk, clr
  Register #(.width(17)) register_48 (.Q(_55a));  // open: D, en, clk, clr
  Register #(.width(32)) register_49 (.Q(_3));  // open: D, en, clk, clr
  Register #(.width(17)) register_50 (.Q(_3a));  // open: D, en, clk, clr
  Register #(.width(32)) register_51 (.Q(_11));  // open: D, en, clk, clr
  Register #(.width(17)) register_52 (.Q(_11a));  // open: D, en, clk, clr
  Register #(.width(32)) register_53 (.Q(_19));  // open: D, en, clk, clr
  Register #(.width(17)) register_54 (.Q(_19a));  // open: D, en, clk, clr
  Register #(.width(32)) register_55 (.Q(_27));  // open: D, en, clk, clr
  Register #(.width(17)) register_56 (.Q(_8a));  // open: D, en, clk, clr
  Register #(.width(32)) register_57 (.Q(_35));  // open: D, en, clk, clr
  Register #(.width(17)) register_58 (.Q(_35a));  // open: D, en, clk, clr
  Register #(.width(32)) register_59 (.Q(_42));  // open: D, en, clk, clr
  Register #(.width(17)) register_60 (.Q(_42a));  // open: D, en, clk, clr
  Register #(.width(32)) register_61 (.Q(_49));  // open: D, en, clk, clr
  Register #(.width(17)) register_62 (.Q(_49a));  // open: D, en, clk, clr
  Register #(.width(32)) register_63 (.Q(_56));  // open: D, en, clk, clr
  Register #(.width(17)) register_64 (.Q(_56a));  // open: D, en, clk, clr
  Register #(.width(32)) register_65 (.Q(_4));  // open: D, en, clk, clr
  Register #(.width(17)) register_66 (.Q(_4a));  // open: D, en, clk, clr
  Register #(.width(32)) register_67 (.Q(_12));  // open: D, en, clk, clr
  Register #(.width(17)) register_68 (.Q(_12a));  // open: D, en, clk, clr
  Register #(.width(32)) register_69 (.Q(_20));  // open: D, en, clk, clr
  Register #(.width(17)) register_70 (.Q(_20a));  // open: D, en, clk, clr
  Register #(.width(32)) register_71 (.Q(_28));  // open: D, en, clk, clr
  Register #(.width(17)) register_72 (.Q(_28a));  // open: D, en, clk, clr
  Register #(.width(32)) register_73 (.Q(_36));  // open: D, en, clk, clr
  Register #(.width(17)) register_74 (.Q(_36a));  // open: D, en, clk, clr
  Register #(.width(32)) register_75 (.Q(_43));  // open: D, en, clk, clr
  Register #(.width(17)) register_76 (.Q(_43a));  // open: D, en, clk, clr
  Register #(.width(32)) register_77 (.Q(_50));  // open: D, en, clk, clr
  Register #(.width(17)) register_78 (.Q(_50a));  // open: D, en, clk, clr
  Register #(.width(32)) register_79 (.Q(_57));  // open: D, en, clk, clr
  Register #(.width(17)) register_80 (.Q(_57a));  // open: D, en, clk, clr
  Register #(.width(32)) register_81 (.Q(_5));  // open: D, en, clk, clr
  Register #(.width(17)) register_82 (.Q(_5a));  // open: D, en, clk, clr
  Register #(.width(32)) register_83 (.Q(_13));  // open: D, en, clk, clr
  Register #(.width(17)) register_84 (.Q(_13a));  // open: D, en, clk, clr
  Register #(.width(32)) register_85 (.Q(_21));  // open: D, en, clk, clr
  Register #(.width(17)) register_86 (.Q(_21a));  // open: D, en, clk, clr
  Register #(.width(32)) register_87 (.Q(_29));  // open: D, en, clk, clr
  Register #(.width(17)) register_88 (.Q(_29a));  // open: D, en, clk, clr
  Register #(.width(32)) register_89 (.Q(_37));  // open: D, en, clk, clr
  Register #(.width(17)) register_90 (.Q(_37a));  // open: D, en, clk, clr
  Register #(.width(32)) register_91 (.Q(_44));  // open: D, en, clk, clr
  Register #(.width(17)) register_92 (.Q(_44a));  // open: D, en, clk, clr
  Register #(.width(32)) register_93 (.Q(_51));  // open: D, en, clk, clr
  Register #(.width(17)) register_94 (.Q(_51a));  // open: D, en, clk, clr
  Register #(.width(32)) register_95 (.Q(_58));  // open: D, en, clk, clr
  Register #(.width(17)) register_96 (.Q(_58a));  // open: D, en, clk, clr
  Register #(.width(32)) register_97 (.Q(_6));  // open: D, en, clk, clr
  Register #(.width(17)) register_98 (.Q(_6a));  // open: D, en, clk, clr
  Register #(.width(32)) register_99 (.Q(_14));  // open: D, en, clk, clr
  Register #(.width(17)) register_100 (.Q(_14a));  // open: D, en, clk, clr
  Register #(.width(32)) register_101 (.Q(_22));  // open: D, en, clk, clr
  Register #(.width(17)) register_102 (.Q(_22a));  // open: D, en, clk, clr
  Register #(.width(32)) register_103 (.Q(_30));  // open: D, en, clk, clr
  Register #(.width(17)) register_104 (.Q(_30a));  // open: D, en, clk, clr
  Register #(.width(32)) register_105 (.Q(_38));  // open: D, en, clk, clr
  Register #(.width(17)) register_106 (.Q(_38a));  // open: D, en, clk, clr
  Register #(.width(32)) register_107 (.Q(_45));  // open: D, en, clk, clr
  Register #(.width(17)) register_108 (.Q(_45a));  // open: D, en, clk, clr
  Register #(.width(32)) register_109 (.Q(_52));  // open: D, en, clk, clr
  Register #(.width(17)) register_110 (.Q(_52a));  // open: D, en, clk, clr
  Register #(.width(32)) register_111 (.Q(_59));  // open: D, en, clk, clr
  Register #(.width(17)) register_112 (.Q(_59a));  // open: D, en, clk, clr
  Register #(.width(32)) register_113 (.Q(_7));  // open: D, en, clk, clr
  Register #(.width(17)) register_114 (.Q(_7a));  // open: D, en, clk, clr
  Register #(.width(32)) register_115 (.Q(_15));  // open: D, en, clk, clr
  Register #(.width(17)) register_116 (.Q(_15a));  // open: D, en, clk, clr
  Register #(.width(32)) register_117 (.Q(_23));  // open: D, en, clk, clr
  Register #(.width(17)) register_118 (.Q(_23a));  // open: D, en, clk, clr
  Register #(.width(32)) register_119 (.Q(_31));  // open: D, en, clk, clr
  Register #(.width(17)) register_120 (.Q(_31a));  // open: D, en, clk, clr
  Register #(.width(32)) register_121 (.Q(_60));  // open: D, en, clk, clr
  Register #(.width(17)) register_122 (.Q(_60a));  // open: D, en, clk, clr
  Register #(.width(32)) register_123 (.Q(_61));  // open: D, en, clk, clr
  Register #(.width(17)) register_124 (.Q(_61a));  // open: D, en, clk, clr
  Register #(.width(32)) register_125 (.Q(_62));  // open: D, en, clk, clr
  Register #(.width(17)) register_126 (.Q(_62a));  // open: D, en, clk, clr
  Register #(.width(32)) register_127 (.Q(_63));  // open: D, en, clk, clr
  Register #(.width(17)) register_128 (.Q(_63a));  // open: D, en, clk, clr
  Multiplexer #(.select(5), .width(32), .enable("false")) multiplexer_1 (
    .in0(_0), .in1(_1), .in2(_2), .in3(_3), .in4(_4), .in5(_5), .in6(_6), .in7(_7), .in8(_8), .in9(_9),
    .in10(_10), .in11(_11), .in12(_12), .in13(_13), .in14(_14), .in15(_15), .in16(_16), .in17(_17),
    .in18(_18), .in19(_19), .in20(_20), .in21(_21), .in22(_22), .in23(_23), .in24(_24), .in25(_25),
    .in26(_26), .in27(_27), .in28(_28), .in29(_29), .in30(_30), .in31(_31), .out(multiplexer_1_out),
    .sel({a4, a3, a2, a1, a0}));
  Multiplexer #(.select(5), .width(32), .enable("false")) multiplexer_2 (
    .in0(_32), .in1(_33), .in2(_34), .in3(_35), .in4(_36), .in5(_37), .in6(_38), .in7(_39), .in8(_40),
    .in9(_41), .in10(_42), .in11(_43), .in12(_44), .in13(_45), .in14(_46), .in15(_47), .in16(_48),
    .in17(_49), .in18(_50), .in19(_51), .in20(_52), .in21(_53), .in22(_54), .in23(_55), .in24(_56),
    .in25(_57), .in26(_58), .in27(_59), .in28(_60), .in29(_61), .in30(_62), .in31(_63),
    .out(multiplexer_2_out), .sel({a4, a3, a2, a1, a0}));
  Multiplexer #(.width(32), .enable("false")) multiplexer_3 (
    .in0(multiplexer_1_out), .in1(multiplexer_2_out), .out(out1), .sel(a5));
  Multiplexer #(.select(5), .width(17), .enable("false")) multiplexer_4 (
    .in0(_0a), .in1(_1a), .in2(_2a), .in3(_3a), .in4(_4a), .in5(_5a), .in6(_6a), .in7(_7a), .in8(_8a),
    .in9(_9a), .in10(_10a), .in11(_11a), .in12(_12a), .in13(_13a), .in14(_14a), .in15(_15a), .in16(_16a),
    .in17(_17a), .in18(_18a), .in19(_19a), .in20(_20a), .in21(_21a), .in22(_22a), .in23(_23a), .in24(_24a),
    .in25(_25a), .in26(_26a), .in27(_27a), .in28(_28a), .in29(_29a), .in30(_30a), .in31(_31a),
    .out(multiplexer_4_out), .sel({a4, a3, a2, a1, a0}));
  Multiplexer #(.select(5), .width(17), .enable("false")) multiplexer_5 (
    .in0(_32a), .in1(_33a), .in2(_34a), .in3(_35a), .in4(_36a), .in5(_37a), .in6(_38a), .in7(_39a),
    .in8(_40a), .in9(_41a), .in10(_42a), .in11(_43a), .in12(_44a), .in13(_45a), .in14(_46a), .in15(_47a),
    .in16(_48a), .in17(_49a), .in18(_50a), .in19(_51a), .in20(_52a), .in21(_53a), .in22(_54a), .in23(_55a),
    .in24(_56a), .in25(_57a), .in26(_58a), .in27(_59a), .in28(_60a), .in29(_61a), .in30(_62a), .in31(_63a),
    .out(multiplexer_5_out), .sel({a4, a3, a2, a1, a0}));
  Multiplexer #(.width(17), .enable("false")) multiplexer_6 (
    .in0(multiplexer_4_out), .in1(multiplexer_5_out), .out(out2), .sel(a5));

  // Notes on the sheet:
  //   000000
  //   001000
  //   010000
  //   011000
  //   100000
  //   100111
  //   101110
  //   110101
  //   000001
  //   010001
  //   011001
  //   100001
  //   101000
  //   101111
  //   110110
  //   001001
  //   011010
  //   110000
  //   110111
  //   000010
  //   001010
  //   010010
  //   100010
  //   101001
  //   000011
  //   001011
  //   010011
  //   011011
  //   100011
  //   101010
  //   110001
  //   111000
  //   000100
  //   001100
  //   010100
  //   011100
  //   100100
  //   101011
  //   110010
  //   111001
  //   000101
  //   001101
  //   010101
  //   011101
  //   100101
  //   101100
  //   110011
  //   111010
  //   010110
  //   011110
  //   100110
  //   101101
  //   110100
  //   111011
  //   000110
  //   001110
  //   001111
  //   111100
  //   000111
  //   010111
  //   011111
  //   111101
  //   111110
  //   111111
endmodule
